// Logisim project cpuproj.circ as structural Verilog: 1 circuit, main circuit main
module main (
  output [7:0] RegData1,
  output [7:0] ReadDataM,
  output [7:0] RegData2,
  output [7:0] RegDataW
);

  wire and_1_out, and_2_out, and_3_out, and_4_out, and_5_out, decoder_1_out0, decoder_1_out1, decoder_1_out2,
       decoder_1_out3, not_1_out, not_2_out, not_3_out, or_1_out, or_2_out, TheClock_out, xor_1_out;
  wire [1:0] multiplexer_1_out, ram_1_dout_2;
  wire [7:0] adder_1_out, adder_2_out, multiplexer_4_out, multiplexer_5_out, PC_q, register_1_q,
       subtractor_1_out, X0_q, X1_q, X2_q, X3_q;
  wire [7:2] ram_1_dout;

  Clock TheClock (.out(TheClock_out));
  Register PC (.D(adder_1_out), .en(1'b1), .clk(TheClock_out), .Q(PC_q));  // open: clr
  RAM #(.enables("line")) ram_1 (.addr(PC_q), .clk(TheClock_out), .dout({ram_1_dout, ram_1_dout_2}));  // open: we, din
  Adder adder_1 (.a(PC_q), .b(8'h1), .out(adder_1_out));  // open: cin, cout
  not not_1 (not_1_out, ram_1_dout[7]);
  xor xor_1 (xor_1_out, ram_1_dout[6], ram_1_dout[7]);
  or or_1 (or_1_out, ram_1_dout[6], ram_1_dout[7]);
  or or_2 (or_2_out, ram_1_dout[6], not_1_out);
  Multiplexer #(.width(2)) multiplexer_1 (
    .in0(ram_1_dout_2), .in1(ram_1_dout[5:4]), .out(multiplexer_1_out), .sel(xor_1_out));
  Decoder #(.select(2)) decoder_1 (
    .out0(decoder_1_out0), .out1(decoder_1_out1), .out2(decoder_1_out2), .out3(decoder_1_out3),
    .sel(multiplexer_1_out));  // open: en
  and and_1 (and_1_out, ram_1_dout[7], xor_1_out);
  not not_2 (not_2_out, xor_1_out);
  and and_2 (and_2_out, or_2_out, decoder_1_out0);
  and and_3 (and_3_out, or_2_out, decoder_1_out1);
  and and_4 (and_4_out, or_2_out, decoder_1_out2);
  and and_5 (and_5_out, or_2_out, decoder_1_out3);
  Register X0 (.D(RegDataW), .en(and_2_out), .clk(TheClock_out), .Q(X0_q));  // open: clr
  Register X1 (.D(RegDataW), .en(and_3_out), .clk(TheClock_out), .Q(X1_q));  // open: clr
  Register X2 (.D(RegDataW), .en(and_4_out), .clk(TheClock_out), .Q(X2_q));  // open: clr
  Register X3 (.D(RegDataW), .en(and_5_out), .clk(TheClock_out), .Q(X3_q));  // open: clr
  Multiplexer #(.select(2), .width(8)) multiplexer_2 (
    .in0(X0_q), .in1(X1_q), .in2(X2_q), .in3(X3_q), .out(RegData1), .sel(ram_1_dout[5:4]));
  Multiplexer #(.select(2), .width(8)) multiplexer_3 (
    .in0(X0_q), .in1(X1_q), .in2(X2_q), .in3(X3_q), .out(RegData2), .sel(ram_1_dout[3:2]));
  Multiplexer #(.width(8)) multiplexer_4 (
    .in0(RegData1), .in1({{6{1'b0}}, ram_1_dout_2}), .out(multiplexer_4_out), .sel(xor_1_out));
  Adder adder_2 (.a(multiplexer_4_out), .b(RegData2), .out(adder_2_out));  // open: cin, cout
  Subtractor subtractor_1 (.a(RegData1), .b(RegData2), .out(subtractor_1_out));  // open: bin, bout
  not not_3 (not_3_out, or_1_out);
  Multiplexer #(.width(8)) multiplexer_5 (
    .in0(adder_2_out), .in1(subtractor_1_out), .out(multiplexer_5_out), .sel(not_3_out));
  Register register_1 (.D(multiplexer_5_out), .en(1'b1), .clk(TheClock_out), .Q(register_1_q));  // open: clr
  RAM #(.enables("line")) ram_2 (
    .addr(register_1_q), .we(and_1_out), .clk(TheClock_out), .din(RegData1), .dout(ReadDataM));
  Multiplexer #(.width(8)) multiplexer_6 (.in0(ReadDataM), .in1(multiplexer_5_out), .out(RegDataW), .sel(not_2_out));

  // Notes on the sheet:
  //   opcode
  //   1st Reg
  //   ADD:11 LDR 01 STR 10 SUB 00
  //   2nd Reg or Target
  //   Reg 2
  //   Reg1
  //   to choose immediate
  //   3rd reg or dest reg
  //   if its immidate
  //   if its desreg
  //   writeenable
  //   to choose if Write enable should be on for memory
  //   Register File
  //   readreg1
  //   readreg2
  //   ts wirte for the imm
  //   ALU
  //   str wont work because m3 has to be 1 for str to work
  //   write enable has to be on to write into memeory
  //   Data Memory
  //   this will calc the offset right now its just offsetting by 1
  //   have to choose when to use the aluout vs the stuff from the memory in the case of add it should just skip the memeory 
endmodule
